# Fritzing sketch Schaltplan-WRO (saved by Fritzing 0.9.10b)
breadboards: 1

parts:
  Raspberry_Pi_1 = Raspberry Pi 3 [part_number=RPI-3-V1.2]
  HC-SR04_Sensor_1 = HC-SR04 Ultrasonic Distance Sensor
  HC-SR04_Sensor_2 = HC-SR04 Ultrasonic Distance Sensor
  HC-SR04_Sensor_3 = HC-SR04 Ultrasonic Distance Sensor
  J1 = Basic Servo
  GyroSensor = InvenSense MPU6050
  R1 = Resistor [tolerance=±5% power=0.25 resistance=330 package=THT]
  R5 = Resistor [tolerance=±5% power=0.25 resistance=330 package=THT]
  R6 = Resistor [tolerance=±5% power=0.25 resistance=330 package=THT]
  R7 = Resistor [tolerance=±5% power=0.25 resistance=470 package=THT]
  R8 = Resistor [tolerance=±5% power=0.25 resistance=470 package=THT]
  R9 = Resistor [tolerance=±5% power=0.25 resistance=470 package=THT]

nets:
  N1: Raspberry_Pi_1.GPIO2, GyroSensor.SDA
  N2: Raspberry_Pi_1.GPIO3, GyroSensor.SCL
  3V3: Raspberry_Pi_1.3V3, GyroSensor.VCC
  N3: Raspberry_Pi_1.ID_SD, R6.Pin_1, R9.Pin_0
  N4: Raspberry_Pi_1.GIPO26, J1.pulse
  GND: Raspberry_Pi_1.GND, HC-SR04_Sensor_1.GND, HC-SR04_Sensor_2.GND, HC-SR04_Sensor_3.GND, J1.gnd, GyroSensor.GND, R7.Pin_1, R8.Pin_1, R9.Pin_1
  N5: Raspberry_Pi_1.GIPO21, R5.Pin_1, R8.Pin_0
  N6: Raspberry_Pi_1.GIPO20, HC-SR04_Sensor_2.TRIG
  N7: Raspberry_Pi_1.GIPO16, R7.Pin_0
  N8: Raspberry_Pi_1.GIPO12, HC-SR04_Sensor_3.TRIG
  N9: Raspberry_Pi_1.ID_SC, HC-SR04_Sensor_1.TRIG
  VCC: Raspberry_Pi_1.5V, HC-SR04_Sensor_1.VCC, HC-SR04_Sensor_2.VCC, HC-SR04_Sensor_3.VCC, J1.vcc
  N10: HC-SR04_Sensor_1.ECHO, R6.Pin_0
  N11: HC-SR04_Sensor_2.ECHO, R5.Pin_0
  N12: HC-SR04_Sensor_3.ECHO, R1.Pin_0
